# Fritzing sketch FINAL-PROJECT (saved by Fritzing 0.8.7b)
breadboards: 1

parts:
  Part1 = Arduino Mega 2560 (Rev3)
  R1 = Resistor [tolerance=±5% resistance=330 package=THT]
  R2 = Resistor [tolerance=±5% resistance=150 package=THT]
  C1 = Electrolytic Capacitor [capacitance=1µF package="100 mil [THT, electrolytic]"]

nets:
  N1: Part1.A0, R1.Pin_0, R2.Pin_1, C1.-
  N2: Part1.D13_PWM, R2.Pin_0
  N3: Part1.D11_PWM, R1.Pin_1
  N4: Part1.GND, C1.+

notes:
  CAPACITANCE METER
  for 1 uF to 3.9 uF capacitors using ARDUINO MEGA 2560 (REV3)
  BUDIONGAN-LIM
  FINAL PROJECT
  1 unknown capacitor
  1 150 OHMS resistor
  1 330 OHMS resistor
