# Fritzing sketch MIDTERM_DELTA_TO_WYE (saved by Fritzing 0.8.7b)
breadboards: 1

parts:
  Part1 = Arduino Mega 2560 (Rev3)
  R1 = Resistor [tolerance=±5% resistance=1k package=THT]
  R2 = Resistor [tolerance=±5% resistance=620 package=THT]
  R3 = Resistor [tolerance=±5% resistance=680 package=THT]
  R4 = Resistor [tolerance=±5% resistance=820 package=THT]

nets:
  N1: Part1.A0, R1.Pin_1, R2.Pin_0
  N2: Part1.A1, R2.Pin_1, R3.Pin_0
  N3: Part1.A2, R3.Pin_1, R4.Pin_0
  N4: Part1.5V, R4.Pin_1
  N5: Part1.GND, R1.Pin_0

notes:
  BUDIONGAN-LIM
  MIDTERM PROJECT
  DELTA-TO-WYE TRANSFORMATION USING ARDUINO MEGA 2560 (REV3)
  RESISTORS USED:
  1-1K OHMS (KNOWN RESISTOR)
  1- 620 OHMS RESISTOR
  1- 680 OHMS RESISTOR
  1- 820 OHMS RESISTOR
